# Fritzing sketch SoundBoardPCB (saved by Fritzing 0.9.3b)
circuit board: 4.6cm x 5.2cm
breadboards: 1

parts:
  Part1 = Arduino Pro Mini v13
  DFRobot_DFPlayer_Mini1 = DFRobot DFPlayer Mini [part_number=DFR0299]
  Audio_out = molex pin header, 3 pins [form=molex]
  R1 = Resistor [tolerance=±5% resistance=220 package=THT]
  R2 = Resistor [tolerance=±5% resistance=220 package=THT]
  Power = molex pin header, 2 pins [form=molex]
  Power_LED = molex pin header, 2 pins [form=molex]
  R3 = Resistor [tolerance=±5% resistance=220 package=THT]
  Speaker_3w = molex pin header, 2 pins [form=molex]  # not connected

nets:
  N1: Part1.RAW, Power.pin2
  N2: Part1.GND, Power.pin1, Power_LED.pin1
  VCC: Part1.VCC, DFRobot_DFPlayer_Mini1.VCC, R3.Pin_0
  N3: Part1.D11_PWM/MOSI, R2.Pin_0
  N4: Part1.D10_PWM/SS, R1.Pin_0
  N5: DFRobot_DFPlayer_Mini1.RX, R1.Pin_1
  N6: DFRobot_DFPlayer_Mini1.TX, R2.Pin_1
  N7: DFRobot_DFPlayer_Mini1.DAC_R, Audio_out.pin2
  N8: DFRobot_DFPlayer_Mini1.DAC_L, Audio_out.pin3
  N9: DFRobot_DFPlayer_Mini1.GND-1, DFRobot_DFPlayer_Mini1.GND-2, Audio_out.pin1
  N10: Power_LED.pin2, R3.Pin_1
